# Fritzing sketch braco-robo-completo (saved by Fritzing 0.9.10b)
breadboards: 1

parts:
  Componente1 = Arduino Uno (Rev3) - ICSP
  Componente2 = Thumb Joystick
  Componente3 = Thumb Joystick
  J1 = Basic Servo
  J2 = Basic Servo
  J3 = Basic Servo
  J4 = Basic Servo

nets:
  N1: Componente1.A0, Componente2.HORZ
  N2: Componente1.A1, Componente2.VERT
  VCC: Componente1.A2, Componente1.A3, Componente1.5V, Componente3.X, Componente3.Y, Componente3.VCC, J1.vcc, J2.vcc, J3.vcc, J4.vcc
  N3: Componente1.D9_PWM, J3.pulse
  N4: Componente1.D10_PWM/SS, J4.pulse
  N5: Componente1.D5_PWM, J1.pulse
  N6: Componente1.D6_PWM, J2.pulse
  GND: Componente1.GND, Componente2.GND, Componente3.GND, J1.gnd, J2.gnd, J3.gnd, J4.gnd

notes:
  JOYSTICK2
  JOYSTICK1
  BASE
  BRAÇO1
  BRAÇO2
  GARRA

custom parts:
  Thumb Joystick: Description: This is the breakout board for the thumb joystick. Pins are broken out to a 0.1" header and includes 4 mounting holes in the corners. Dimensions: 1" x 1.25"
